// Digital circuit BinMind.dig as structural Verilog
module BinMind (
  input  Foam_food_containers,
  input  Snack_wrappers__chip_bags,
  input  Used_tissue_paper,
  input  Dirty_materials_that_can_t_be_cleaned,
  input  Face_masks__sanitary_pads,
  input  Food_scraps,
  input  Vegetable_and_fruit_peels,
  input  Rice_leftovers__fish_bones,
  input  Eggshells__coffee_grounds,
  input  Wilted_flowers_or_leaves,
  input  Clean_plastic_bottles__PET,
  input  Aluminum_cans,
  input  Clean_paper_and_cardboard,
  input  Glass_bottles_and_jars,
  input  Milk_or_juice_cartons__washed,
  input  Batteries,
  input  Pesticides,
  input  Fluorescent_bulbs,
  input  Cleaning_chemicals,
  input  Electronic_waste,
  input  Align_G,
  input  Align_W,
  input  Align_R
);

  wire and_1_out, and_2_out, and_3_out, and_4_out, and_5_out, and_6_out, and_7_out, and_8_out, and_9_out,
       and_10_out, and_11_out, and_12_out, and_13_out, and_14_out, and_15_out, and_16_out, not_1_out,
       not_2_out, not_3_out, not_4_out, not_5_out, not_6_out, not_7_out, or_1_out, or_2_out, or_3_out,
       or_4_out, or_5_out, or_6_out, or_7_out, or_8_out;

  or or_1 (or_1_out, Foam_food_containers, Snack_wrappers__chip_bags, Used_tissue_paper, Dirty_materials_that_can_t_be_cleaned, Face_masks__sanitary_pads);
  or or_2 (or_2_out, Food_scraps, Vegetable_and_fruit_peels, Rice_leftovers__fish_bones, Eggshells__coffee_grounds, Wilted_flowers_or_leaves);
  or or_3 (or_3_out, Clean_plastic_bottles__PET, Aluminum_cans, Clean_paper_and_cardboard, Glass_bottles_and_jars, Milk_or_juice_cartons__washed);
  or or_4 (or_4_out, Batteries, Pesticides, Fluorescent_bulbs, Cleaning_chemicals, Electronic_waste);
  not not_1 (not_1_out, or_1_out);
  not not_2 (not_2_out, or_2_out);
  not not_3 (not_3_out, or_3_out);
  not not_4 (not_4_out, or_4_out);
  or or_5 (or_5_out, or_1_out, or_3_out);
  and and_1 (and_1_out, or_2_out, not_1_out, not_3_out);
  and and_2 (and_2_out, or_3_out, not_1_out, not_2_out);
  not not_5 (not_5_out, Align_G);
  not not_6 (not_6_out, Align_W);
  not not_7 (not_7_out, Align_R);
  and and_3 (and_3_out, not_2_out, or_1_out, or_3_out);
  and and_4 (and_4_out, or_2_out, or_5_out);
  and and_5 (and_5_out, or_1_out, not_2_out, not_3_out);
  and and_6 (and_6_out, and_1_out, not_4_out);
  and and_7 (and_7_out, and_2_out, not_4_out);
  and and_8 (and_8_out, and_14_out, not_5_out);
  and and_9 (and_9_out, and_6_out, not_6_out);
  and and_10 (and_10_out, and_7_out, not_7_out);
  and and_11 (and_11_out, and_14_out, Align_G);
  and and_12 (and_12_out, and_6_out, Align_W);
  and and_13 (and_13_out, and_7_out, Align_R);
  or or_6 (or_6_out, and_3_out, and_4_out, and_5_out);
  or or_7 (or_7_out, and_8_out, and_9_out, and_10_out);
  or or_8 (or_8_out, and_11_out, and_12_out, and_13_out);
  and and_14 (and_14_out, or_6_out, not_4_out);
  and and_15 (and_15_out, or_7_out, not_4_out);
  and and_16 (and_16_out, or_8_out, not_4_out);
  LED General (.in(and_14_out));
  LED Wet (.in(and_6_out));
  LED Recycle (.in(and_7_out));
  LED Hazardous (.in(or_4_out));
  LED Rotate (.in(and_15_out));
  LED Trap_door (.in(and_16_out));
  LED Buzz (.in(or_4_out));

  // Notes on the sheet:
  //   General Waste
  //   Wet Waste
  //   Recyclable Waste
  //   Hazardous Waste
  //   General logic case
  //   Wet logic case
  //   Recyclable logic case
  //   Sensor
  //   G+R
  //   W*~G*~R
  //   R*~G*~W
  //   Rotate logic case
  //   Trap door logic case
  //   ~W*G*R
  //   W*(G+R)
  //   G*~W*~R
  //   ~H*(W*~G*~R)
  //   ~H*(R*~G*~W)
  //   General*~Align_G
  //   Wet*~Align_W
  //   Recycle*~Align_R
  //   General*Align_G
  //   Wet*Align_W
  //   Recycle*Align_R
  //   (~W*G*R)+(W*(G+R))+(G*~W*~R)
  //   ~H*[ (~W*G*R)+(W*(G+R))+(G*~W*~R) ]
  //   ~Align
  //   Align
  //   ~Align*~H
  //   Align*~H
  //   Output
  //   System
endmodule
